// Logisim project s-mips.circ as structural Verilog: 14 circuits, main circuit S-MIPS Board
module S_MIPS_Board (
  input  DESHABILITAR_DISPATCHER,
  output halt
);

  wire button_1_out, CLK, CS, d_ff_1_q, LCLR, LoadRAM, LoadRAMOn, LW, R_R_W, R_W, ram_dispatcher_1_finished,
       RCS, Reset_out, RST, TTY_EN;
  wire [2:0] KDB;
  wire [3:0] LMask, Mask, ram_1_read_time, ram_1_write_time, RMask;
  wire [6:0] KDB_DATA, TTY_DATA;
  wire [15:0] Addr, LAddr, RAddr;
  wire [31:0] I0, I1, I2, I3, LData, ram_1_data_out_0, ram_1_data_out_1, ram_1_data_out_2, ram_1_data_out_3,
       RI0, RI1, RI2, RI3;

  TTY #(.rows(25), .cols(80)) tty_1 (.data(TTY_DATA), .clk(CLK), .we(TTY_EN), .clr(RST));
  not not_1 (LoadRAMOn, ram_dispatcher_1_finished);
  RAM_Dispatcher ram_dispatcher_1 (
    .WriteTime(ram_1_write_time), .Clock(CLK), .Data(LData), .Address(LAddr), .Mask(LMask),
    .Finished(ram_dispatcher_1_finished), .Write(LW), .CLR(LCLR));
  Keyboard #(.buflen(64)) keyboard_1 (.clk(CLK), .re(KDB[0]), .avail(KDB[2]), .data(KDB_DATA));  // open: clr
  RAM ram_1 (
    .Address(RAddr), .Data_Out_0(ram_1_data_out_0), .Data_Out_1(ram_1_data_out_1),
    .Data_Out_2(ram_1_data_out_2), .Data_Out_3(ram_1_data_out_3), .Data_In_0(RI0), .Data_In_1(RI1),
    .Data_In_2(RI2), .Data_In_3(RI3), .Mask(RMask), .nRead_Write(R_R_W), .Chip_Select(RCS),
    .Read_Time(ram_1_read_time), .Reset(button_1_out), .Write_Time(ram_1_write_time));
  Button button_1 (.out(button_1_out));
  D_Flip_Flop d_ff_1 (.clk(CLK), .D(1'b1), .Q(d_ff_1_q), .reset(Reset_out));  // open: Qn, preset, en
  Button Reset (.out(Reset_out));
  S_MIPS s_mips_1 (
    .Kbd_Enable(KDB[0]), .Address(Addr), .Kbd_Clear(KDB[1]), .Kbd_Available(KDB[2]), .RAM_In_0(I0),
    .Kbd_ASCII_Data(KDB_DATA), .RAM_In_1(I1), .TTY_Enable(TTY_EN), .RAM_In_2(I2), .RAM_In_3(I2),
    .TTY_ASCII_Data(TTY_DATA), .Reset(RST), .RAM_Out_0(ram_1_data_out_0), .Clock(CLK),
    .RAM_Out_1(ram_1_data_out_1), .Stop(halt), .RAM_Out_2(ram_1_data_out_2), .RAM_Out_3(ram_1_data_out_3),
    .Mask(Mask), .Read_Time(ram_1_read_time), .Write_Time(ram_1_write_time), .nRead_Write(R_W),
    .Chip_Select(CS));
  D_Flip_Flop d_ff_2 (.clk(CLK), .D(d_ff_1_q), .Qn(LCLR), .reset(Reset_out));  // open: Q, preset, en
  or or_1 (RST, LCLR, LoadRAM);
  Clock clock_1 (.out(CLK));
  Multiplexer #(.width(32), .enable("false")) multiplexer_1 (.in0(I0), .in1(LData), .out(RI0), .sel(LoadRAM));
  Multiplexer #(.width(32), .enable("false")) multiplexer_2 (.in0(I1), .in1(LData), .out(RI1), .sel(LoadRAM));
  Multiplexer #(.width(32), .enable("false")) multiplexer_3 (.in0(I2), .in1(LData), .out(RI2), .sel(LoadRAM));
  Multiplexer #(.width(32), .enable("false")) multiplexer_4 (.in0(I3), .in1(LData), .out(RI3), .sel(LoadRAM));
  and and_1 (LoadRAM, ~DESHABILITAR_DISPATCHER, LoadRAMOn);  // AND_Gate
  Multiplexer #(.width(16), .enable("false")) multiplexer_5 (.in0(Addr), .in1(LAddr), .out(RAddr), .sel(LoadRAM));
  Multiplexer #(.width(4), .enable("false")) multiplexer_6 (.in0(Mask), .in1(LMask), .out(RMask), .sel(LoadRAM));
  Multiplexer #(.enable("false")) multiplexer_7 (.in0(CS), .in1(LW), .out(RCS), .sel(LoadRAM));
  Multiplexer #(.enable("false")) multiplexer_8 (.in0(R_W), .in1(LW), .out(R_R_W), .sel(LoadRAM));

  // Notes on the sheet:
  //   NO MODIFICAR
  //   Keyboard
endmodule

module S_MIPS (
  input  Kbd_Available,
  input  [6:0] Kbd_ASCII_Data,
  input  [31:0] RAM_Out_0,
  input  [31:0] RAM_Out_1,
  input  Reset,
  input  [31:0] RAM_Out_2,
  input  Clock,
  input  [31:0] RAM_Out_3,
  input  [3:0] Read_Time,
  input  [3:0] Write_Time,
  output Kbd_Enable,
  output [15:0] Address,
  output Kbd_Clear,
  output TTY_Enable,
  output [6:0] TTY_ASCII_Data,
  output Stop,
  output [31:0] RAM_In_0,
  output [31:0] RAM_In_1,
  output [31:0] RAM_In_2,
  output [31:0] RAM_In_3,
  output [3:0] Mask,
  output nRead_Write,
  output Chip_Select
);

  wire instruction_decoder_1_inm, instruction_decoder_1_r, instruction_decoder_1_save,
       instruction_decoder_1_w, JC, JI, Rd;
  wire [4:0] instruction_decoder_1_a, instruction_decoder_1_b, instruction_decoder_1_da, Op;
  wire [31:0] A, B, branch_control_1_output, C, Instr, JS, k, LDLR, multiplexer_1_out, WAddress;

  instruction_decoder instruction_decoder_1 (
    .in_1(Instr), .K(k[25:0]), .jump(JI), .Op(Op), .W(instruction_decoder_1_w),
    .DA(instruction_decoder_1_da), .R(instruction_decoder_1_r), .A(instruction_decoder_1_a),
    .B(instruction_decoder_1_b), .Inm(instruction_decoder_1_inm), .save(instruction_decoder_1_save));
  Register_File register_file_1 (
    .in_1(instruction_decoder_1_da), .in_2(instruction_decoder_1_save), .in_3(C),
    .in_6(instruction_decoder_1_a), .in_4(Clock), .in_7(instruction_decoder_1_b), .A(A), .B(B), .in_5(Reset));
  Cronometro cronometro_1 (
    .in_1(Write_Time), .Start(instruction_decoder_1_r), .Activo(1'b0), .Reloj(Clock), .Enable(Reset),
    .Counting(nRead_Write));  // open: Output
  Cronometro cronometro_2 (
    .in_1(Read_Time), .Start(instruction_decoder_1_w), .Activo(1'b0), .Reloj(Clock), .Enable(Reset),
    .Counting(Rd));  // open: Output
  Branch_control branch_control_1 (
    .Jump_size(JS), .INSTRUC(JI), .COND(JC), .CLK(Clock), .RST(Reset), .Output(branch_control_1_output));
  Multiplexer #(.width(32), .enable("false")) multiplexer_1 (
    .in0(B), .in1(k), .out(multiplexer_1_out), .sel(instruction_decoder_1_inm));
  Program_counter program_counter_1 (
    .in_1(RAM_In_0), .ENTRADAS(Read_Time), .in_8(Rd), .in_2(RAM_In_1), .in_10(nRead_Write), .in_6(RAM_In_2),
    .in_11(RAM_In_3), .in_3(Instr), .in_9(LDLR), .in_4(Clock), .in_7(Reset));
  ALU alu_1 (
    .in_2(A), .in_3(multiplexer_1_out), .Result(C), .in_4(Op), .in_1(Clock), .Cond(JC), .Jump_size(JS),
    .Stop(Stop), .Enable(TTY_Enable), .TTY(TTY_ASCII_Data), .in_7(Kbd_Available), .in_6(Kbd_ASCII_Data),
    .in_5(Reset));
  READ_AND_WRITE read_and_write_1 (
    .in_1(k), .in_2(A), .in_3(Clock), .in_4(Reset), .in_5(B), .in_6(Op), .out_7(RAM_Out_0),
    .out_8(RAM_Out_1), .Output(WAddress), .out_10(RAM_Out_2), .out_11(RAM_Out_3));
  GET_RAM_ADDRESS get_ram_address_1 (
    .in_4(Rd), .in_1(branch_control_1_output), .in_5(WAddress), .RAM_Address(Address), .in_3(nRead_Write));  // open: in_2

  assign Chip_Select = 1'b1;

  // Other names for the same wires on the sheet: CLK = Clock; CLR = Reset; KBD_AVAIL = Kbd_Available;
  //   KBD_CLR = Kbd_Clear; KBD_DATA[6:0] = Kbd_ASCII_Data; RAM_A[15:0] = Address; RAM_INPUT_0[31:0] = RAM_In_0;
  //   RAM_INPUT_1[31:0] = RAM_In_1; RAM_INPUT_2[31:0] = RAM_In_2; RAM_INPUT_3[31:0] = RAM_In_3; RAM_MASK[3:0] = Mask;
  //   RAM_OUTPUT_0[31:0] = RAM_Out_0; RAM_OUTPUT_1[31:0] = RAM_Out_1; RAM_OUTPUT_2[31:0] = RAM_Out_2;
  //   RAM_OUTPUT_3[31:0] = RAM_Out_3; TTY_DATA[6:0] = TTY_ASCII_Data; RW = nRead_Write; Wr = nRead_Write

  // Notes on the sheet:
  //   RAM ADDRESS
  //   DATA FROM RAM
  //   DATA TO RAM
  //   DATA WRITE MASK
  //   RAM TIMING
  //   RAM CONTROL
  //   KEYBOARD
  //   TTY
  //   SEQUENCING
  //   LDLR: Leido de la RAM 
endmodule

module RAM (
  input  [15:0] Address,
  input  [31:0] Data_In_0,
  input  [31:0] Data_In_1,
  input  [31:0] Data_In_2,
  input  [31:0] Data_In_3,
  input  [3:0] Mask,
  input  nRead_Write,
  input  Chip_Select,
  input  Reset,
  output [31:0] Data_Out_0,
  output [31:0] Data_Out_1,
  output [31:0] Data_Out_2,
  output [31:0] Data_Out_3,
  output [3:0] Read_Time,
  output [3:0] Write_Time
);

  wire and_2_out, and_3_out, and_4_out, and_5_out, and_6_out, and_7_out, and_8_out, and_9_out, Changed, CLK,
       comparator_2_eq, comparator_3_eq, comparator_4_eq, comparator_5_eq, comparator_6_eq, Count,
       demultiplexer_3_out0, Idle, Idle_q, Load, Load0, Load1, nand_1_out, or_1_out, or_2_out, or_3_out,
       or_4_out, or_5_out, or_6_out, or_7_out, or_8_out, or_9_out, or_10_out, Proc_q, Update_Mem, Zero_Time;
  wire [3:0] counter_1_q, multiplexer_1_out, subtractor_1_out;
  wire [31:0] register_1_q, register_2_q, register_3_q, register_4_q, register_5_q;

  // Probe on 4'b0011
  // Probe on 4'b0010
  Multiplexer #(.width(4), .enable("false")) multiplexer_1 (
    .in0(4'b0011), .in1(4'b0010), .out(multiplexer_1_out), .sel(nRead_Write));
  or or_1 (or_1_out, Idle, Update_Mem);
  or or_2 (or_2_out, ~Chip_Select, Reset);  // OR_Gate
  Subtractor #(.width(4)) subtractor_1 (.a(multiplexer_1_out), .b(4'b0010), .out(subtractor_1_out));  // open: bin, bout
  D_Flip_Flop u_Idle (.clk(CLK), .D(or_1_out), .Q(Idle_q), .preset(or_2_out));  // open: Qn, en, reset
  Demultiplexer #(.enable("false")) demultiplexer_1 (.out0(Idle), .out1(Load0), .in(Idle_q), .sel(Changed));
  // Probe on counter_1_q
  Counter #(.width(4), .max('hf)) counter_1 (
    .load(Load), .D(subtractor_1_out), .count(Count), .Q(counter_1_q), .clk(CLK), .clr(or_3_out));  // open: carry
  or or_3 (or_3_out, ~Chip_Select, Reset);  // OR_Gate
  Comparator #(.width(4), .mode("unsigned")) comparator_1 (
    .a(4'b0000), .b(counter_1_q), .eq(Zero_Time));  // open: gt, lt
  or or_4 (or_4_out, Count, Load0, Load1);
  Register #(.width(32)) register_1 (.D(Data_In_0), .en(Chip_Select), .Q(register_1_q), .clk(CLK), .clr(or_5_out));
  or or_5 (or_5_out, ~Chip_Select, Reset);  // OR_Gate
  Register #(.width(32)) register_2 (.D(Data_In_1), .en(Chip_Select), .Q(register_2_q), .clk(CLK), .clr(or_6_out));
  or or_6 (or_6_out, ~Chip_Select, Reset);  // OR_Gate
  Register #(.width(32)) register_3 (.D(Data_In_2), .en(Chip_Select), .Q(register_3_q), .clk(CLK), .clr(or_7_out));
  or or_7 (or_7_out, ~Chip_Select, Reset);  // OR_Gate
  Register #(.width(32)) register_4 (.D(Data_In_3), .en(Chip_Select), .Q(register_4_q), .clk(CLK), .clr(or_8_out));
  or or_8 (or_8_out, ~Chip_Select, Reset);  // OR_Gate
  Register #(.width(32)) register_5 (
    .D({{11{1'b1}}, nRead_Write, Mask, Address}), .en(Chip_Select), .Q(register_5_q), .clk(CLK),
    .clr(or_9_out));
  or or_9 (or_9_out, ~Chip_Select, Reset);  // OR_Gate
  D_Flip_Flop Proc (.clk(CLK), .D(or_4_out), .Q(Proc_q), .reset(or_10_out));  // open: Qn, preset, en
  or or_10 (or_10_out, ~Chip_Select, Reset);  // OR_Gate
  Demultiplexer #(.enable("false")) demultiplexer_2 (
    .out0(Count), .out1(Update_Mem), .in(demultiplexer_3_out0), .sel(Zero_Time));
  Demultiplexer #(.enable("false")) demultiplexer_3 (
    .out0(demultiplexer_3_out0), .out1(Load1), .in(Proc_q), .sel(Changed));
  Clock clock_1 (.out(CLK));
  Comparator #(.width(32)) comparator_2 (.a(register_1_q), .b(Data_In_0), .eq(comparator_2_eq));  // open: gt, lt
  Comparator #(.width(32)) comparator_3 (.a(register_2_q), .b(Data_In_1), .eq(comparator_3_eq));  // open: gt, lt
  Comparator #(.width(32)) comparator_4 (.a(register_3_q), .b(Data_In_2), .eq(comparator_4_eq));  // open: gt, lt
  Comparator #(.width(32)) comparator_5 (.a(register_4_q), .b(Data_In_3), .eq(comparator_5_eq));  // open: gt, lt
  Comparator #(.width(32)) comparator_6 (
    .a(register_5_q), .b({{11{1'b1}}, nRead_Write, Mask, Address}), .eq(comparator_6_eq));  // open: gt, lt
  nand nand_1 (nand_1_out, comparator_6_eq, comparator_2_eq, comparator_3_eq, comparator_4_eq, comparator_5_eq);
  and and_1 (Changed, nand_1_out, Chip_Select);
  or or_11 (Load, Count, Load1, Load0);
  and and_2 (and_2_out, Mask[0], Update_Mem, nRead_Write);
  and and_3 (and_3_out, Mask[1], Update_Mem, nRead_Write);
  and and_4 (and_4_out, Mask[2], Update_Mem, nRead_Write);
  and and_5 (and_5_out, Mask[3], Update_Mem, nRead_Write);
  RAM_part #(.addrWidth(16), .dataWidth(32), .bus("separate")) ram_1 (
    .addr(Address), .din(Data_In_0), .data(Data_Out_0), .str(and_2_out), .sel(Chip_Select), .clk(CLK),
    .ld(and_6_out), .clr(Reset));
  and and_6 (and_6_out, ~nRead_Write, Idle);  // AND_Gate
  RAM_part #(.addrWidth(16), .dataWidth(32), .bus("separate")) ram_2 (
    .addr(Address), .din(Data_In_1), .data(Data_Out_1), .str(and_3_out), .sel(Chip_Select), .clk(CLK),
    .ld(and_7_out), .clr(Reset));
  and and_7 (and_7_out, ~nRead_Write, Idle);  // AND_Gate
  RAM_part #(.addrWidth(16), .dataWidth(32), .bus("separate")) ram_3 (
    .addr(Address), .din(Data_In_2), .data(Data_Out_2), .str(and_4_out), .sel(Chip_Select), .clk(CLK),
    .ld(and_8_out), .clr(Reset));
  and and_8 (and_8_out, ~nRead_Write, Idle);  // AND_Gate
  RAM_part #(.addrWidth(16), .dataWidth(32), .bus("separate")) ram_4 (
    .addr(Address), .din(Data_In_3), .data(Data_Out_3), .str(and_5_out), .sel(Chip_Select), .clk(CLK),
    .ld(and_9_out), .clr(Reset));
  and and_9 (and_9_out, ~nRead_Write, Idle);  // AND_Gate

  assign Read_Time = 4'b0011;
  assign Write_Time = 4'b0010;

  // Other names for the same wires on the sheet: M0 = Mask[0]; M1 = Mask[1]; M2 = Mask[2]; M3 = Mask[3];
  //   RW = nRead_Write; CLR = Reset; CS = Chip_Select; Load2 = Count

  // Notes on the sheet:
  //   NO MODIFICAR
  //   excepto quizás los valores RT y WT
  //   BANK0
  //   BANK1
  //   BANK2
  //   BANK3
endmodule

module RAM_Dispatcher (
  input  [3:0] WriteTime,
  input  Clock,
  input  CLR,
  output [31:0] Data,
  output [15:0] Address,
  output [3:0] Mask,
  output Finished,
  output Write
);

  wire demultiplexer_2_out1, demultiplexer_3_out1, End, IDLE_q, IncAddr, Load, or_1_out, or_2_out, While_q,
       WriteEnd;
  wire [3:0] counter_1_q;
  wire [31:0] CurrentAddress_q;

  Counter #(.width(32), .max('hffffffff)) CurrentAddress (
    .count(IncAddr), .Q({CurrentAddress_q[31:18], Address, CurrentAddress_q[1:0]}), .clk(Clock), .clr(CLR));  // open: load, D, carry
  or or_1 (or_1_out, IncAddr, demultiplexer_3_out1, Finished);
  D_Flip_Flop IDLE (.clk(Clock), .D(or_1_out), .Q(IDLE_q), .preset(CLR));  // open: Qn, en, reset
  Demultiplexer #(.enable("false")) demultiplexer_1 (.out0(Load), .out1(Finished), .in(IDLE_q), .sel(End));
  D_Flip_Flop While (.clk(Clock), .D(or_2_out), .Q(While_q), .reset(CLR));  // open: Qn, preset, en
  or or_2 (or_2_out, Write, Load);
  RAM_part #(.addrWidth(18), .dataWidth(32)) ram_1 (
    .addr({Address, CurrentAddress_q[1:0]}), .data(Data), .clk(Clock));  // open: sel, ld, clr
  Demultiplexer #(.enable("false")) demultiplexer_2 (
    .out0(Write), .out1(demultiplexer_2_out1), .in(While_q), .sel(WriteEnd));
  Decoder #(.select(2)) decoder_1 (
    .out0(Mask[0]), .out1(Mask[1]), .out2(Mask[2]), .out3(Mask[3]), .sel(CurrentAddress_q[1:0]));  // open: en
  Demultiplexer #(.enable("false")) demultiplexer_3 (
    .out0(IncAddr), .out1(demultiplexer_3_out1), .in(demultiplexer_2_out1), .sel(End));
  Counter #(.width(4), .max('hf)) counter_1 (
    .load(Load), .D(WriteTime), .count(Write), .Q(counter_1_q), .clk(Clock));  // open: carry, clr
  Comparator #(.width(32)) comparator_1 (.a(Data), .b({32{1'b1}}), .eq(End));  // open: gt, lt
  Comparator #(.width(4)) comparator_2 (.a(4'b0000), .b(counter_1_q), .eq(WriteEnd));  // open: gt, lt

  // Other names for the same wires on the sheet: CLK = Clock; Count = Write; WT[3:0] = WriteTime
endmodule

// Saca 1 cuando termino de cargar la instruccion
module Program_counter (
  input  [31:0] in_1,
  input  [31:0] in_2,
  input  [31:0] in_3,
  input  in_4,
  input  [3:0] ENTRADAS,
  input  [31:0] in_6,
  input  in_7,
  input  in_8,
  input  [31:0] in_9,
  input  in_10,
  input  [31:0] in_11
);

  wire Enable, reading;

  Multiplexer #(.width(32), .enable("false")) multiplexer_1 (
    .in0(32'h1000ffff), .in1({in_3[31:16], in_2[7:0], in_1[7:0]}), .out(in_9), .sel(reading));
  Cronometro cronometro_1 (
    .in_1(ENTRADAS), .Activo(1'b1), .Output(reading), .Reloj(in_4), .Enable(Enable));  // open: Start, Counting
  or or_1 (Enable, in_7, in_8, in_10);

  assign in_3[15:0] = {in_2[7:0], in_1[7:0]};
  assign in_6[7:0] = in_3[23:16];
  assign in_11[7:0] = in_3[31:24];

  // Other names for the same wires on the sheet: CLK = in_4; RT[3:0] = ENTRADAS

  // Notes on the sheet:
  //   B0
  //   B1
  //   B2
  //   B3
  //   PROGRAM COUNTER
  //   1 cuando termina de cargar la instruccion
  //   Ciclo infinito para ignorar ordenes
  //   READED FROM RAM
  //   NEXT INSTRUCTION
endmodule

module Borrador (
  input  [3:0] in_1,
  input  Start,
  input  Activo,
  input  Enable,
  output Output,
  output Counting
);

  wire clock_1_out, comparator_1_gt, comparator_1_lt, comparator_2_lt, or_1_out, or_2_out, or_3_out,
       or_4_out, t_ff_1_q;
  wire [4:0] counter_1_q;

  or or_1 (or_1_out, Output, Start);
  Clock clock_1 (.out(clock_1_out));
  T_Flip_Flop t_ff_1 (.clk(clock_1_out), .T(or_1_out), .Q(t_ff_1_q));  // open: Qn, preset, reset, en
  or or_2 (or_2_out, t_ff_1_q, Activo);
  Counter #(.width(5), .max('h1f)) counter_1 (
    .count(or_2_out), .Q(counter_1_q), .clk(clock_1_out), .clr(or_3_out));  // open: load, D, carry
  Comparator #(.width(5)) comparator_1 (
    .a(counter_1_q), .b({5{1'b0}}), .gt(comparator_1_gt), .lt(comparator_1_lt));  // open: eq
  Comparator #(.width(5)) comparator_2 (
    .a({1'b0, in_1}), .b(counter_1_q), .eq(Output), .lt(comparator_2_lt));  // open: gt
  or or_3 (or_3_out, comparator_2_lt, Enable);
  or or_4 (or_4_out, comparator_1_gt, comparator_1_lt, Start);
  and and_1 (Counting, ~Enable, or_4_out);  // AND_Gate
endmodule

module Cronometro (
  input  [3:0] in_1,
  input  Start,
  input  Activo,
  input  Enable,
  input  Reloj,
  output Output,
  output Counting
);

  wire comparator_1_gt, comparator_1_lt, comparator_2_lt, or_1_out, or_2_out, or_3_out, t_ff_1_q;
  wire [4:0] counter_1_q;

  or or_1 (or_1_out, Output, Start);
  T_Flip_Flop t_ff_1 (.clk(Reloj), .T(or_1_out), .Q(t_ff_1_q));  // open: Qn, preset, reset, en
  or or_2 (or_2_out, t_ff_1_q, Activo);
  Counter #(.width(5), .max('h1f)) counter_1 (
    .count(or_2_out), .Q(counter_1_q), .clk(Reloj), .clr(or_3_out));  // open: load, D, carry
  Comparator #(.width(5)) comparator_1 (
    .a(counter_1_q), .b({5{1'b0}}), .gt(comparator_1_gt), .lt(comparator_1_lt));  // open: eq
  Comparator #(.width(5)) comparator_2 (
    .a({1'b0, in_1}), .b(counter_1_q), .eq(Output), .lt(comparator_2_lt));  // open: gt
  or or_3 (or_3_out, comparator_2_lt, Enable);
  or or_4 (Counting, comparator_1_gt, comparator_1_lt, Start);

  // Notes on the sheet:
  //   Cronometro: Devuelve 1 cuando pasan
  //   Tantos ciclos de reloj
  //   Como indica la entrada
endmodule

module GET_RAM_ADDRESS (
  input  [31:0] in_1,
  input  [31:0] in_2,
  input  in_3,
  input  in_4,
  input  [31:0] in_5,
  output [15:0] RAM_Address
);

  wire [31:16] multiplexer_1_out;

  Multiplexer #(.select(2), .width(32)) multiplexer_1 (
    .in0(in_1), .in1(in_2), .in2(in_5), .out({multiplexer_1_out, RAM_Address}), .sel({in_3, in_4}));  // open: in3, en

  // Notes on the sheet:
  //   CB INSTRUCTION
  //   READ INSTRUCTION
  //   WRITE INSTRUCTION
  //   RAM ADDRESS
endmodule

module instruction_decoder (
  input  [31:0] in_1,
  output jump,
  output save,
  output [4:0] Op,
  output [4:0] DA,
  output W,
  output [4:0] B,
  output [4:0] A,
  output R,
  output [25:0] K,
  output Inm
);

  wire add, \and , and_1_out, and_6_out, and_13_out, and_14_out, and_15_out, and_16_out, and_18_out,
       and_19_out, beq, bgtz, blez, bltz, bne, comparator_1_lt, comparator_2_eq, comparator_3_gt,
       comparator_4_eq, comparator_5_eq, comparator_6_eq, comparator_7_eq, comparator_8_eq, comparator_9_eq,
       comparator_10_eq, comparator_13_lt, comparator_14_eq, comparator_15_eq, comparator_18_eq,
       comparator_19_eq, comparator_20_eq, comparator_22_eq, comparator_23_lt, comparator_24_gt,
       comparator_24_lt, comparator_25_gt, comparator_26_eq, comparator_27_eq, comparator_28_eq,
       comparator_30_eq, comparator_31_eq, comparator_32_eq, comparator_33_eq, comparator_34_eq,
       comparator_35_eq, comparator_36_eq, comparator_38_eq, comparator_39_eq, comparator_42_eq,
       comparator_43_eq, comparator_44_eq, comparator_45_eq, comparator_46_eq, comparator_48_eq,
       comparator_49_eq, div, divu, halt, j, jr, kbd, lw, mfhi, mflo, mul, mulu, \nor , not_1_out, not_2_out,
       OPCODE_0, \or , or_2_out, or_4_out, or_8_out, pop, push, rnd, stl, stlu, sub, sw, tty, xnor_1_out,
       xnor_2_out, \xor ;
  wire [9:0] undriven;
  wire [15:0] I_Constant;

  Comparator #(.width(6)) comparator_1 (.a(6'b001111), .b(in_1[31:26]), .lt(comparator_1_lt));  // open: gt, eq
  Comparator #(.width(6)) comparator_2 (.a(in_1[31:26]), .b(6'b001001), .eq(comparator_2_eq));  // open: gt, lt
  Comparator #(.width(6)) comparator_3 (.a(in_1[31:26]), .b(6'b000111), .gt(comparator_3_gt));  // open: eq, lt
  Comparator #(.width(11)) comparator_4 (.a(11'h20), .b(in_1[10:0]), .eq(comparator_4_eq));  // open: gt, lt
  Comparator #(.width(6)) comparator_5 (.a(6'b001000), .b(in_1[31:26]), .eq(comparator_5_eq));  // open: gt, lt
  Comparator #(.width(16)) comparator_6 (.a(16'h18), .b(in_1[15:0]), .eq(comparator_6_eq));  // open: gt, lt
  Comparator #(.width(16)) comparator_7 (.a(16'h1a), .b(in_1[15:0]), .eq(comparator_7_eq));  // open: gt, lt
  Comparator #(.width(11)) comparator_8 (.a(11'h12), .b(in_1[10:0]), .eq(comparator_8_eq));  // open: gt, lt
  Comparator #(.width(16)) comparator_9 (.a({16{1'b0}}), .b(in_1[31:16]), .eq(comparator_9_eq));  // open: gt, lt
  Comparator #(.width(11)) comparator_10 (.a(11'h12), .b(in_1[10:0]), .eq(comparator_10_eq));  // open: gt, lt
  Comparator #(.width(6)) comparator_11 (.a(6'b000100), .b(in_1[31:26]), .eq(beq));  // open: gt, lt
  Comparator #(.width(6)) comparator_12 (.a(6'b000101), .b(in_1[31:26]), .eq(bne));  // open: gt, lt
  not not_1 (not_1_out, comparator_2_eq);
  and and_1 (and_1_out, OPCODE_0, comparator_4_eq);
  and and_2 (mul, OPCODE_0, comparator_6_eq);
  and and_3 (div, OPCODE_0, comparator_7_eq);
  and and_4 (mflo, comparator_8_eq, comparator_9_eq);
  and and_5 (mfhi, comparator_9_eq, comparator_10_eq);
  and and_6 (and_6_out, comparator_1_lt, not_1_out, comparator_3_gt);
  or or_1 (add, and_1_out, comparator_5_eq);
  Multiplexer #(.width(5), .enable("false")) multiplexer_1 (
    .in0(in_1[20:16]), .in1(in_1[15:11]), .out(DA), .sel(and_6_out));
  Comparator #(.width(32)) comparator_13 (.a(in_1), .b(32'hfc00003f), .eq(halt), .lt(comparator_13_lt));  // open: gt
  Comparator #(.width(6)) comparator_14 (.a({6{1'b1}}), .b(in_1[31:26]), .eq(comparator_14_eq));  // open: gt, lt
  Comparator #(.width(21)) comparator_15 (.a(21'h1), .b(in_1[20:0]), .eq(comparator_15_eq));  // open: gt, lt
  Comparator #(.width(6)) comparator_16 (.a(6'b000110), .b(in_1[31:26]), .eq(blez));  // open: gt, lt
  Comparator #(.width(6)) comparator_17 (.a(6'b000111), .b(in_1[31:26]), .eq(bgtz));  // open: gt, lt
  Comparator #(.width(11)) comparator_18 (.a(11'h22), .b(in_1[10:0]), .eq(comparator_18_eq));  // open: gt, lt
  Comparator #(.width(16)) comparator_19 (.a(16'h19), .b(in_1[15:0]), .eq(comparator_19_eq));  // open: gt, lt
  Comparator #(.width(16)) comparator_20 (.a(16'h1b), .b(in_1[15:0]), .eq(comparator_20_eq));  // open: gt, lt
  and and_7 (tty, comparator_14_eq, comparator_15_eq);
  Comparator #(.width(6)) comparator_21 (.a(in_1[31:26]), .b({6{1'b0}}), .eq(OPCODE_0));  // open: gt, lt
  and and_8 (sub, OPCODE_0, comparator_18_eq);
  and and_9 (mulu, OPCODE_0, comparator_19_eq);
  and and_10 (divu, OPCODE_0, comparator_20_eq);
  Comparator #(.width(16)) comparator_22 (.a(16'hfc00), .b(in_1[31:16]), .eq(comparator_22_eq));  // open: gt, lt
  Comparator #(.width(6)) comparator_23 (.a(6'b001000), .b(in_1[31:26]), .lt(comparator_23_lt));  // open: gt, eq
  Comparator #(.width(6)) comparator_24 (
    .a(in_1[31:26]), .b(6'b000011), .gt(comparator_24_gt), .lt(comparator_24_lt));  // open: eq
  Comparator #(.width(6)) comparator_25 (.a(in_1[31:26]), .b({6{1'b0}}), .gt(comparator_25_gt));  // open: eq, lt
  and and_11 (rnd, comparator_22_eq, comparator_26_eq);
  Comparator #(.width(11)) comparator_26 (.a(11'h2), .b(in_1[10:0]), .eq(comparator_26_eq));  // open: gt, lt
  Comparator #(.width(16)) comparator_27 (.a(16'hfc00), .b(in_1[31:16]), .eq(comparator_27_eq));  // open: gt, lt
  and and_12 (kbd, comparator_27_eq, comparator_28_eq);
  Comparator #(.width(11)) comparator_28 (.a(11'h3), .b(in_1[10:0]), .eq(comparator_28_eq));  // open: gt, lt
  Comparator #(.width(6)) comparator_29 (.a(6'b000001), .b(in_1[31:26]), .eq(bltz));  // open: gt, lt
  and and_13 (and_13_out, comparator_23_lt, or_2_out, comparator_25_gt);
  or or_2 (or_2_out, comparator_24_gt, comparator_24_lt);
  Multiplexer #(.width(5), .enable("false")) multiplexer_2 (
    .in0(in_1[25:21]), .in1({5{1'b1}}), .out(B), .sel(or_4_out));
  Multiplexer #(.width(26), .enable("false")) multiplexer_3 (
    .in0({undriven, I_Constant}), .in1(in_1[25:0]), .out(K), .sel(j));
  Comparator #(.width(11)) comparator_30 (.a(11'h2a), .b(in_1[10:0]), .eq(comparator_30_eq));  // open: gt, lt
  Comparator #(.width(6)) comparator_31 (.a(6'b001010), .b(in_1[31:26]), .eq(comparator_31_eq));  // open: gt, lt
  Comparator #(.width(11)) comparator_32 (.a(11'h24), .b(in_1[10:0]), .eq(comparator_32_eq));  // open: gt, lt
  Comparator #(.width(6)) comparator_33 (.a(6'b001100), .b(in_1[31:26]), .eq(comparator_33_eq));  // open: gt, lt
  Comparator #(.width(11)) comparator_34 (.a(11'h25), .b(in_1[10:0]), .eq(comparator_34_eq));  // open: gt, lt
  Comparator #(.width(6)) comparator_35 (.a(6'b001101), .b(in_1[31:26]), .eq(comparator_35_eq));  // open: gt, lt
  or or_3 (jump, and_13_out, comparator_36_eq);
  or or_4 (or_4_out, push, pop);
  and and_14 (and_14_out, OPCODE_0, comparator_30_eq);
  and and_15 (and_15_out, OPCODE_0, comparator_32_eq);
  and and_16 (and_16_out, OPCODE_0, comparator_34_eq);
  Comparator #(.width(27)) comparator_36 (
    .a({in_1[31:26], in_1[20:0]}), .b(27'h8), .eq(comparator_36_eq));  // open: gt, lt
  or or_5 (stl, and_14_out, comparator_31_eq);
  or or_6 (\and , and_15_out, comparator_33_eq);
  or or_7 (\or , and_16_out, comparator_35_eq);
  Comparator #(.width(6)) comparator_37 (.a(6'b100011), .b(in_1[31:26]), .eq(lw));  // open: gt, lt
  Comparator #(.width(16)) comparator_38 (.a(16'he000), .b(in_1[31:16]), .eq(comparator_38_eq));  // open: gt, lt
  Comparator #(.width(11)) comparator_39 (.a({11{1'b0}}), .b(in_1[10:0]), .eq(comparator_39_eq));  // open: gt, lt
  Comparator #(.width(6)) comparator_40 (.a(6'b000010), .b(in_1[31:26]), .eq(j));  // open: gt, lt
  Comparator #(.width(21)) comparator_41 (.a(21'h8), .b(in_1[20:0]), .eq(jr));  // open: gt, lt
  and and_17 (pop, comparator_38_eq, comparator_39_eq);
  Priority_Encoder #(.select(5), .disabled(0)) priority_encoder_1 (
    .in0(1'b0), .in1(add), .in2(sub), .in3(mul), .in4(mulu), .in5(div), .in6(divu), .in7(stl), .in8(stlu),
    .in9(\and ), .in10(\or ), .in11(\nor ), .in12(\xor ), .in13(beq), .in14(bne), .in15(blez), .in16(bgtz),
    .in17(bltz), .in18(j), .in19(jr), .in20(mflo), .in21(mfhi), .in22(lw), .in23(sw), .in24(pop),
    .in25(push), .in26(halt), .in27(tty), .in28(rnd), .in29(kbd), .in30(1'b0), .in31(1'b0), .out(Op));  // open: gs, en_out, en_in
  not not_2 (not_2_out, in_1[28]);
  Comparator #(.width(11)) comparator_42 (.a(11'h2b), .b(in_1[10:0]), .eq(comparator_42_eq));  // open: gt, lt
  Comparator #(.width(6)) comparator_43 (.a(6'b001011), .b(in_1[31:26]), .eq(comparator_43_eq));  // open: gt, lt
  Comparator #(.width(11)) comparator_44 (.a(11'h28), .b(in_1[10:0]), .eq(comparator_44_eq));  // open: gt, lt
  Comparator #(.width(6)) comparator_45 (.a(6'b001110), .b(in_1[31:26]), .eq(comparator_45_eq));  // open: gt, lt
  Comparator #(.width(11)) comparator_46 (.a(11'h27), .b(in_1[10:0]), .eq(comparator_46_eq));  // open: gt, lt
  NotExactlyOne xnor_1 (.out(xnor_1_out), .in0(in_1[26]), .in1(in_1[27]), .in2(in_1[28]));
  or or_8 (or_8_out, not_2_out, in_1[29]);
  NotExactlyOne xnor_2 (.out(xnor_2_out), .in0(in_1[29]), .in1(in_1[30]), .in2(in_1[31]));
  and and_18 (and_18_out, OPCODE_0, comparator_42_eq);
  and and_19 (and_19_out, OPCODE_0, comparator_44_eq);
  and and_20 (\nor , OPCODE_0, comparator_46_eq);
  Comparator #(.width(6)) comparator_47 (.a(6'b101011), .b(in_1[31:26]), .eq(sw));  // open: gt, lt
  Comparator #(.width(6)) comparator_48 (.a(6'b111000), .b(in_1[31:26]), .eq(comparator_48_eq));  // open: gt, lt
  Comparator #(.width(21)) comparator_49 (.a(21'h1), .b(in_1[20:0]), .eq(comparator_49_eq));  // open: gt, lt
  nor nor_1 (save, beq, bne, blez, bgtz, bltz, j, jr, sw, push, halt, tty);
  or or_9 (W, sw, push);
  or or_10 (R, lw, pop);
  nand nand_1 (Inm, xnor_1_out, or_8_out, xnor_2_out);
  or or_11 (stlu, and_18_out, comparator_43_eq);
  or or_12 (\xor , and_19_out, comparator_45_eq);
  and and_21 (push, comparator_48_eq, comparator_49_eq);

  assign A = in_1[20:16];

  // Other names for the same wires on the sheet: Big_part_of_it[20:0] = in_1[20:0]; IConstant[15:0] = in_1[15:0];
  //   Instruction[31:0] = in_1; J_Value[25:0] = in_1[25:0]; RD[4:0] = in_1[15:11]; RT[4:0] = in_1[20:16];
  //   Start[15:0] = in_1[31:16]; Op_Code[5:0] = in_1[31:26]; End[10:0] = in_1[10:0]; Func_Code[5:0] = in_1[5:0];
  //   x[4:0] = in_1[10:6]; RS[4:0] = in_1[25:21]

  // Notes on the sheet:
  //   INSTRUCTION
  //   ADD
  //   MUL
  //   DIV
  //   OPERACIONES MOVE
  //   SEPARANDO LA ENTRADA
  //   OPERACIONES ARITMETICAS
  //   MOVE FROM LO
  //   MOVE FROM HI
  //   BEQ
  //   BNE
  //   OBTENIENDO DIRECCION
  //   EN LA CUAL SE ESCRIBE
  //   DECODER
  //   SUB
  //   Halt
  //   OPERACIONES ESPECIALES
  //   MULU
  //   DIVU
  //   TTY
  //   BLEZ
  //   BGTZ
  //   OPERADORES
  //   CONSTANTE k
  //   SET RANDOM
  //   SET KEY
  //   OPERACIONES BRANCH
  //   INSTRUCCION DE SALTO
  //   auxiliares
  //   BLTZ
  //   STL
  //   AND
  //   OR
  //   POP FROM STACK
  //   OPERACIONES JUMP
  //   DA LA OPERACION
  //   READ/WRITE
  //   LOAD W
  //   JUMP
  //   JUMP
  //   REG
  //   STLU
  //   XOR
  //   NOR
  //   PUSH IN STAK
  //   GUARDA EN LOS
  //   REGISTROS
  //   SE ESCRIBIRA
  //   EN LA RAM
  //   SE LEERA DE LA RAM
  //   INMEDIATE
  //   OPERATION
  //   STORE W
endmodule

module Register_File (
  input  [4:0] in_1,
  input  in_2,
  input  [31:0] in_3,
  input  in_4,
  input  in_5,
  input  [4:0] in_6,
  input  [4:0] in_7,
  output [31:0] A,
  output [31:0] B
);

  wire and_1_out, and_2_out, and_3_out, and_4_out, and_5_out, and_6_out, and_7_out, and_8_out, and_9_out,
       and_10_out, and_11_out, and_12_out, and_13_out, and_14_out, and_15_out, and_16_out, and_17_out,
       and_18_out, and_19_out, and_20_out, and_21_out, and_22_out, and_23_out, and_24_out, and_25_out,
       and_26_out, and_27_out, and_28_out, and_29_out, and_30_out, and_31_out, comparator_1_eq,
       comparator_2_eq, comparator_3_eq, comparator_4_eq, comparator_5_eq, comparator_6_eq, comparator_7_eq,
       comparator_8_eq, comparator_9_eq, comparator_10_eq, comparator_11_eq, comparator_12_eq,
       comparator_13_eq, comparator_14_eq, comparator_15_eq, comparator_16_eq, comparator_17_eq,
       comparator_18_eq, comparator_19_eq, comparator_20_eq, comparator_21_eq, comparator_22_eq,
       comparator_23_eq, comparator_24_eq, comparator_25_eq, comparator_26_eq, comparator_27_eq,
       comparator_28_eq, comparator_29_eq, comparator_30_eq, comparator_31_eq;
  wire [31:0] _0, _1, _2, _3, _4, _5, _6, _7, _8, _9, _10, _11, _12, _13, _14, _15, _16, _17, _18, _19, _20,
       _21, _22, _23, _24, _25, _26, _27, _28, _29, _30, _31;

  Comparator #(.width(5)) comparator_1 (.a(in_1), .b({5{1'b1}}), .eq(comparator_1_eq));  // open: gt, lt
  and and_1 (and_1_out, comparator_1_eq, in_2);
  Comparator #(.width(5)) comparator_2 (.a(in_1), .b(5'b00001), .eq(comparator_2_eq));  // open: gt, lt
  and and_2 (and_2_out, comparator_2_eq, in_2);
  Comparator #(.width(5)) comparator_3 (.a(in_1), .b(5'b00110), .eq(comparator_3_eq));  // open: gt, lt
  and and_3 (and_3_out, comparator_3_eq, in_2);
  and and_4 (and_4_out, comparator_4_eq, in_2);
  Comparator #(.width(5)) comparator_4 (.a(in_1), .b(5'b01011), .eq(comparator_4_eq));  // open: gt, lt
  Comparator #(.width(5)) comparator_5 (.a(in_1), .b(5'b10000), .eq(comparator_5_eq));  // open: gt, lt
  and and_5 (and_5_out, comparator_5_eq, in_2);
  and and_6 (and_6_out, comparator_6_eq, in_2);
  Comparator #(.width(5)) comparator_6 (.a(in_1), .b(5'b10101), .eq(comparator_6_eq));  // open: gt, lt
  Comparator #(.width(5)) comparator_7 (.a(in_1), .b(5'b11010), .eq(comparator_7_eq));  // open: gt, lt
  and and_7 (and_7_out, comparator_7_eq, in_2);
  Register #(.width(32)) register_1 (.D(in_3), .en(and_1_out), .Q(_31), .clk(in_4), .clr(in_5));
  Register #(.width(32)) register_2 (.D(in_3), .en(and_2_out), .Q(_1), .clk(in_4), .clr(in_5));
  Register #(.width(32)) register_3 (.D(in_3), .en(and_3_out), .Q(_6), .clk(in_4), .clr(in_5));
  Register #(.width(32)) register_4 (.D(in_3), .en(and_4_out), .Q(_11), .clk(in_4), .clr(in_5));
  Register #(.width(32)) register_5 (.D(in_3), .en(and_5_out), .Q(_16), .clk(in_4), .clr(in_5));
  Register #(.width(32)) register_6 (.D(in_3), .en(and_6_out), .Q(_21), .clk(in_4), .clr(in_5));
  Register #(.width(32)) register_7 (.D(in_3), .en(and_7_out), .Q(_26), .clk(in_4), .clr(in_5));
  Comparator #(.width(5)) comparator_8 (.a(in_1), .b(5'b00010), .eq(comparator_8_eq));  // open: gt, lt
  Comparator #(.width(5)) comparator_9 (.a(in_1), .b(5'b00111), .eq(comparator_9_eq));  // open: gt, lt
  Comparator #(.width(5)) comparator_10 (.a(in_1), .b(5'b01100), .eq(comparator_10_eq));  // open: gt, lt
  Comparator #(.width(5)) comparator_11 (.a(in_1), .b(5'b10001), .eq(comparator_11_eq));  // open: gt, lt
  Comparator #(.width(5)) comparator_12 (.a(in_1), .b(5'b10110), .eq(comparator_12_eq));  // open: gt, lt
  Comparator #(.width(5)) comparator_13 (.a(in_1), .b(5'b11011), .eq(comparator_13_eq));  // open: gt, lt
  Register #(.width(32)) register_8 (.Q(_0), .clk(in_4), .clr(in_5));  // open: D, en
  and and_8 (and_8_out, comparator_8_eq, in_2);
  and and_9 (and_9_out, comparator_9_eq, in_2);
  and and_10 (and_10_out, comparator_10_eq, in_2);
  and and_11 (and_11_out, comparator_11_eq, in_2);
  and and_12 (and_12_out, comparator_12_eq, in_2);
  and and_13 (and_13_out, comparator_13_eq, in_2);
  Register #(.width(32)) register_9 (.D(in_3), .en(and_8_out), .Q(_2), .clk(in_4), .clr(in_5));
  Register #(.width(32)) register_10 (.D(in_3), .en(and_9_out), .Q(_7), .clk(in_4), .clr(in_5));
  Register #(.width(32)) register_11 (.D(in_3), .en(and_10_out), .Q(_12), .clk(in_4), .clr(in_5));
  Register #(.width(32)) register_12 (.D(in_3), .en(and_11_out), .Q(_17), .clk(in_4), .clr(in_5));
  Register #(.width(32)) register_13 (.D(in_3), .en(and_12_out), .Q(_22), .clk(in_4), .clr(in_5));
  Register #(.width(32)) register_14 (.D(in_3), .en(and_13_out), .Q(_27), .clk(in_4), .clr(in_5));
  Comparator #(.width(5)) comparator_14 (.a(in_1), .b(5'b00011), .eq(comparator_14_eq));  // open: gt, lt
  Comparator #(.width(5)) comparator_15 (.a(in_1), .b(5'b01000), .eq(comparator_15_eq));  // open: gt, lt
  Comparator #(.width(5)) comparator_16 (.a(in_1), .b(5'b01101), .eq(comparator_16_eq));  // open: gt, lt
  Comparator #(.width(5)) comparator_17 (.a(in_1), .b(5'b10010), .eq(comparator_17_eq));  // open: gt, lt
  Comparator #(.width(5)) comparator_18 (.a(in_1), .b(5'b10111), .eq(comparator_18_eq));  // open: gt, lt
  Comparator #(.width(5)) comparator_19 (.a(in_1), .b(5'b11100), .eq(comparator_19_eq));  // open: gt, lt
  Multiplexer #(.select(5), .width(32)) multiplexer_1 (
    .in0(_0), .in1(_1), .in2(_2), .in3(_3), .in4(_4), .in5(_5), .in6(_6), .in7(_7), .in8(_8), .in9(_9),
    .in10(_10), .in11(_11), .in12(_12), .in13(_13), .in14(_14), .in15(_15), .in16(_16), .in17(_17),
    .in18(_18), .in19(_19), .in20(_20), .in21(_21), .in22(_22), .in23(_23), .in24(_24), .in25(_25),
    .in26(_26), .in27(_27), .in28(_28), .in29(_29), .in30(_30), .in31(_31), .out(A), .sel(in_6));  // open: en
  Register #(.width(32)) register_15 (.D(in_3), .en(and_14_out), .Q(_3), .clk(in_4), .clr(in_5));
  and and_14 (and_14_out, comparator_14_eq, in_2);
  Register #(.width(32)) register_16 (.D(in_3), .en(and_15_out), .Q(_8), .clk(in_4), .clr(in_5));
  and and_15 (and_15_out, comparator_15_eq, in_2);
  Register #(.width(32)) register_17 (.D(in_3), .en(and_16_out), .Q(_13), .clk(in_4), .clr(in_5));
  and and_16 (and_16_out, comparator_16_eq, in_2);
  Register #(.width(32)) register_18 (.D(in_3), .en(and_17_out), .Q(_18), .clk(in_4), .clr(in_5));
  and and_17 (and_17_out, comparator_17_eq, in_2);
  Register #(.width(32)) register_19 (.D(in_3), .en(and_18_out), .Q(_23), .clk(in_4), .clr(in_5));
  and and_18 (and_18_out, comparator_18_eq, in_2);
  Register #(.width(32)) register_20 (.D(in_3), .en(and_19_out), .Q(_28), .clk(in_4), .clr(in_5));
  and and_19 (and_19_out, comparator_19_eq, in_2);
  Comparator #(.width(5)) comparator_20 (.a(in_1), .b(5'b00100), .eq(comparator_20_eq));  // open: gt, lt
  and and_20 (and_20_out, comparator_20_eq, in_2);
  Comparator #(.width(5)) comparator_21 (.a(in_1), .b(5'b01001), .eq(comparator_21_eq));  // open: gt, lt
  and and_21 (and_21_out, comparator_21_eq, in_2);
  Comparator #(.width(5)) comparator_22 (.a(in_1), .b(5'b01110), .eq(comparator_22_eq));  // open: gt, lt
  and and_22 (and_22_out, comparator_22_eq, in_2);
  and and_23 (and_23_out, comparator_23_eq, in_2);
  Comparator #(.width(5)) comparator_23 (.a(in_1), .b(5'b10011), .eq(comparator_23_eq));  // open: gt, lt
  Comparator #(.width(5)) comparator_24 (.a(in_1), .b(5'b11000), .eq(comparator_24_eq));  // open: gt, lt
  and and_24 (and_24_out, comparator_24_eq, in_2);
  Comparator #(.width(5)) comparator_25 (.a(in_1), .b(5'b11101), .eq(comparator_25_eq));  // open: gt, lt
  and and_25 (and_25_out, comparator_25_eq, in_2);
  Multiplexer #(.select(5), .width(32)) multiplexer_2 (
    .in0(_0), .in1(_1), .in2(_2), .in3(_3), .in4(_4), .in5(_5), .in6(_6), .in7(_7), .in8(_8), .in9(_9),
    .in10(_10), .in11(_11), .in12(_12), .in13(_13), .in14(_14), .in15(_15), .in16(_16), .in17(_17),
    .in18(_18), .in19(_19), .in20(_20), .in21(_21), .in22(_22), .in23(_23), .in24(_24), .in25(_25),
    .in26(_26), .in27(_27), .in28(_28), .in29(_29), .in30(_30), .in31(_31), .out(B), .sel(in_7));  // open: en
  Register #(.width(32)) register_21 (.D(in_3), .en(and_20_out), .Q(_4), .clk(in_4), .clr(in_5));
  Register #(.width(32)) register_22 (.D(in_3), .en(and_21_out), .Q(_9), .clk(in_4), .clr(in_5));
  Register #(.width(32)) register_23 (.D(in_3), .en(and_22_out), .Q(_14), .clk(in_4), .clr(in_5));
  Register #(.width(32)) register_24 (.D(in_3), .en(and_23_out), .Q(_19), .clk(in_4), .clr(in_5));
  Register #(.width(32)) register_25 (.D(in_3), .en(and_24_out), .Q(_24), .clk(in_4), .clr(in_5));
  Register #(.width(32)) register_26 (.D(in_3), .en(and_25_out), .Q(_29), .clk(in_4), .clr(in_5));
  Comparator #(.width(5)) comparator_26 (.a(in_1), .b(5'b00101), .eq(comparator_26_eq));  // open: gt, lt
  Comparator #(.width(5)) comparator_27 (.a(in_1), .b(5'b01010), .eq(comparator_27_eq));  // open: gt, lt
  Comparator #(.width(5)) comparator_28 (.a(in_1), .b(5'b01111), .eq(comparator_28_eq));  // open: gt, lt
  Comparator #(.width(5)) comparator_29 (.a(in_1), .b(5'b10100), .eq(comparator_29_eq));  // open: gt, lt
  Comparator #(.width(5)) comparator_30 (.a(in_1), .b(5'b11001), .eq(comparator_30_eq));  // open: gt, lt
  Comparator #(.width(5)) comparator_31 (.a(in_1), .b(5'b11110), .eq(comparator_31_eq));  // open: gt, lt
  Register #(.width(32)) register_27 (.D(in_3), .en(and_26_out), .Q(_5), .clk(in_4), .clr(in_5));
  and and_26 (and_26_out, comparator_26_eq, in_2);
  Register #(.width(32)) register_28 (.D(in_3), .en(and_27_out), .Q(_10), .clk(in_4), .clr(in_5));
  and and_27 (and_27_out, comparator_27_eq, in_2);
  Register #(.width(32)) register_29 (.D(in_3), .en(and_28_out), .Q(_15), .clk(in_4), .clr(in_5));
  and and_28 (and_28_out, comparator_28_eq, in_2);
  Register #(.width(32)) register_30 (.D(in_3), .en(and_29_out), .Q(_20), .clk(in_4), .clr(in_5));
  and and_29 (and_29_out, comparator_29_eq, in_2);
  Register #(.width(32)) register_31 (.D(in_3), .en(and_30_out), .Q(_25), .clk(in_4), .clr(in_5));
  and and_30 (and_30_out, comparator_30_eq, in_2);
  Register #(.width(32)) register_32 (.D(in_3), .en(and_31_out), .Q(_30), .clk(in_4), .clr(in_5));
  and and_31 (and_31_out, comparator_31_eq, in_2);

  // Other names for the same wires on the sheet: AD[4:0] = in_1; CLK = in_4; Input_value[31:0] = in_3; RST = in_5;
  //   RW = in_2; SA[4:0] = in_6; SB[4:0] = in_7

  // Notes on the sheet:
  //   INPUTS
  //   REGISTER FILE
  //   REG:31 (SP)
  //   REG:1
  //   REG:6
  //   REG:11
  //   REG:16
  //   REG:21
  //   REG:26
  //   REG:0
  //   REG:2
  //   REG:7
  //   REG:12
  //   REG:17
  //   REG:22
  //   REG:27
  //   REG:3
  //   REG:8
  //   REG:13
  //   REG:18
  //   REG:23
  //   REG:28
  //   REG:4
  //   REG:9
  //   REG:14
  //   REG:19
  //   REG:24
  //   REG:29
  //   REG:5
  //   REG:10
  //   REG:15
  //   REG:20
  //   REG:25
  //   REG:30
  //   Outputs
endmodule

module ALU (
  input  in_1,
  input  [31:0] in_2,
  input  [31:0] in_3,
  input  [4:0] in_4,
  input  in_5,
  input  [6:0] in_6,
  input  in_7,
  output [6:0] TTY,
  output Stop,
  output Enable,
  output Cond,
  output [31:0] Result,
  output [31:0] Jump_size
);

  wire beq, bgtz, blez, bltz, bne, comparator_3_eq, comparator_4_lt, comparator_5_gt, MOD;
  wire [6:0] KBD_DD;
  wire [31:0] addResult, andResult, HI, kbd, LO, mfhiResult, mfloResult, norResult, orResult, rndResult,
       stlResult, stluResult, subResult, xorResult;

  Comparator #(.width(32)) comparator_1 (.a(in_2), .b(in_3), .eq(beq));  // open: gt, lt
  not not_1 (bne, beq);
  not not_2 (blez, bgtz);
  Comparator #(.width(32)) comparator_2 (.a(in_2), .b({32{1'b0}}), .gt(bgtz), .lt(bltz));  // open: eq
  Multiplexer #(.width(32), .enable("false")) multiplexer_1 (
    .in0(in_3), .in1(in_2), .out(Jump_size), .sel(comparator_3_eq));
  Comparator #(.width(5)) comparator_3 (.a(5'b10011), .b(in_4), .eq(comparator_3_eq));  // open: gt, lt
  Multiplexer #(.select(5), .enable("false")) multiplexer_2 (
    .in0(1'b0), .in1(1'b0), .in2(1'b0), .in3(1'b0), .in4(1'b0), .in5(1'b0), .in6(1'b0), .in7(1'b0),
    .in8(1'b0), .in9(1'b0), .in10(1'b0), .in11(1'b0), .in12(beq), .in13(bne), .in14(blez), .in15(bgtz),
    .in16(bltz), .in17(1'b1), .in18(1'b1), .in19(1'b0), .in20(1'b0), .in21(1'b0), .in22(1'b0), .in23(1'b0),
    .in24(1'b0), .in25(1'b0), .in26(1'b0), .in27(1'b0), .in28(1'b0), .in29(1'b0), .in30(1'b0), .in31(1'b0),
    .out(Cond), .sel(in_4));
  Multiplexer #(.select(5), .width(32), .enable("false")) multiplexer_3 (
    .in0({32{1'b0}}), .in1(addResult), .in2(subResult), .in3({32{1'b0}}), .in4({32{1'b0}}), .in5({32{1'b0}}),
    .in6({32{1'b0}}), .in7(stlResult), .in8(stluResult), .in9(andResult), .in10(orResult), .in11(norResult),
    .in12(xorResult), .in13({32{1'b0}}), .in14({32{1'b0}}), .in15({32{1'b0}}), .in16({32{1'b0}}),
    .in17({32{1'b0}}), .in18({32{1'b0}}), .in19({32{1'b0}}), .in20(mfloResult), .in21(mfhiResult),
    .in22({32{1'b0}}), .in23({32{1'b0}}), .in24({32{1'b0}}), .in25({32{1'b0}}), .in26({32{1'b0}}),
    .in28(rndResult), .in29(kbd), .in30({32{1'b0}}), .in31({32{1'b0}}), .out(Result), .sel(in_4));  // open: in27
  operaciones_logicas operaciones_logicas_1 (.A(in_2), .B(in_3), .OR(orResult), .AND(andResult), .XOR(xorResult));
  Comparator #(.width(5)) comparator_4 (.a(5'b00111), .b(in_4), .lt(comparator_4_lt));  // open: gt, eq
  Comparator #(.width(5)) comparator_5 (.a(in_4), .b(5'b00010), .gt(comparator_5_gt));  // open: eq, lt
  Comparator #(.width(5)) comparator_6 (.a(5'b11011), .b(in_4), .eq(Enable));  // open: gt, lt
  Divider #(.width(32)) divider_1 (.a(in_2), .b(in_3), .out(HI), .upper(LO));  // open: rem
  Register #(.width(32)) register_1 (.D(HI), .en(MOD), .Q(mfhiResult), .clk(in_1), .clr(in_5));
  and and_1 (MOD, comparator_4_lt, comparator_5_gt);
  Adder #(.width(32)) adder_1 (.a(in_2), .b(in_3), .out(addResult));  // open: cin, cout
  Comparator #(.width(32)) comparator_7 (.a(in_2), .b(in_3), .lt(stlResult[0]));  // open: gt, eq
  Multiplexer #(.width(7), .enable("false")) multiplexer_4 (.in0({7{1'b1}}), .in1(KBD_DD), .out(kbd[6:0]), .sel(in_7));
  Register #(.width(32)) register_2 (.D(LO), .en(MOD), .Q(mfhiResult), .clk(in_1), .clr(in_5));
  Subtractor #(.width(32)) subtractor_1 (.a(in_2), .b(in_3), .out(addResult));  // open: bin, bout
  Comparator #(.width(32), .mode("unsigned")) comparator_8 (.a(in_2), .b(in_3), .lt(stlResult[0]));  // open: gt, eq
  Random #(.width(32)) random_1 (.clk(in_1), .next(1'b1), .out(rndResult));  // open: clr
  Comparator #(.width(5)) comparator_9 (.a(5'b11010), .b(in_4), .eq(Stop));  // open: gt, lt

  assign TTY = in_2[6:0];

  // Other names for the same wires on the sheet: A[31:0] = in_2; B[31:0] = in_3; CLK = in_1; KBD_AVAILABLE = in_7;
  //   KBDD[6:0] = in_6; op[4:0] = in_4; RST = in_5

  // Notes on the sheet:
  //   ALU
  //   MULTIPLICACION
  //   ver bien despues
  //   Salida para Branch control
  //   DIVISION
  //   ver bien despues
  //   Entrada
  //   MULTIPLICACION O DIVISION
  //   Salida para Register File
  //   MULTIPLICACION(U)
  //   ver bien despues
  //   CARGAR/GUARDAR HI
  //   SUMA
  //   SET LESS THAN
  //   DIVISION(U)
  //   TTY
  //   OPERACIONES ESPECIALES
  //   OPERACIONES ARITMETICAS Y LOGICAS
  //   REGISTROS AUXILIARES
  //   KBD
  //   CARGAR/GUARDAR LO
  //   RESTA
  //   SET LESS THAN(U)
  //   RND
  //   STOP
endmodule

module operaciones_logicas (
  input  [31:0] A,
  input  [31:0] B,
  output [31:0] OR,
  output [31:0] AND,
  output [31:0] XOR
);

  and and_1 (AND[0], A[0], B[0]);
  and and_2 (AND[1], A[1], B[1]);
  and and_3 (AND[2], A[2], B[2]);
  and and_4 (AND[3], A[3], B[3]);
  and and_5 (AND[4], A[4], B[4]);
  and and_6 (AND[5], A[5], B[5]);
  and and_7 (AND[6], A[6], B[6]);
  and and_8 (AND[7], A[7], B[7]);
  and and_9 (AND[8], A[8], B[8]);
  and and_10 (AND[9], A[9], B[9]);
  and and_11 (AND[10], A[10], B[10]);
  and and_12 (AND[11], A[11], B[11]);
  and and_13 (AND[12], A[12], B[12]);
  and and_14 (AND[13], A[13], B[13]);
  and and_15 (AND[14], A[14], B[14]);
  and and_16 (AND[15], A[15], B[15]);
  and and_17 (AND[16], A[16], B[16]);
  and and_18 (AND[17], A[17], B[17]);
  and and_19 (AND[18], A[18], B[18]);
  and and_20 (AND[19], A[19], B[19]);
  and and_21 (AND[20], A[20], B[20]);
  and and_22 (AND[21], A[21], B[21]);
  and and_23 (AND[22], A[22], B[22]);
  and and_24 (AND[23], A[23], B[23]);
  or or_1 (XOR[0], A[0], B[0]);
  or or_2 (XOR[1], A[1], B[1]);
  or or_3 (XOR[2], A[2], B[2]);
  or or_4 (XOR[3], A[3], B[3]);
  or or_5 (XOR[4], A[4], B[4]);
  or or_6 (XOR[5], A[5], B[5]);
  or or_7 (XOR[6], A[6], B[6]);
  or or_8 (XOR[7], A[7], B[7]);
  and and_25 (AND[24], A[24], B[24]);
  and and_26 (AND[25], A[24], B[24]);
  and and_27 (AND[26], A[25], B[25]);
  and and_28 (AND[27], A[26], B[26]);
  and and_29 (AND[28], A[27], B[28]);
  and and_30 (AND[29], A[29], B[29]);
  and and_31 (AND[30], A[30], B[30]);
  and and_32 (AND[31], A[31], B[31]);
  or or_9 (XOR[8], A[8], B[8]);
  or or_10 (XOR[9], A[9], B[9]);
  or or_11 (XOR[10], A[10], B[10]);
  or or_12 (XOR[11], A[11], B[11]);
  or or_13 (XOR[12], A[12], B[12]);
  or or_14 (XOR[13], A[13], B[13]);
  or or_15 (XOR[14], A[14], B[14]);
  or or_16 (XOR[15], A[15], B[15]);
  or or_17 (OR[0], A[0], B[0]);
  or or_18 (OR[1], A[1], B[1]);
  or or_19 (OR[2], A[2], B[2]);
  or or_20 (OR[3], A[3], B[3]);
  or or_21 (OR[4], A[4], B[4]);
  or or_22 (OR[5], A[5], B[5]);
  or or_23 (OR[6], A[6], B[6]);
  or or_24 (OR[7], A[7], B[7]);
  or or_25 (XOR[16], A[16], B[16]);
  or or_26 (XOR[17], A[17], B[17]);
  or or_27 (XOR[18], A[18], B[18]);
  or or_28 (XOR[19], A[19], B[19]);
  or or_29 (XOR[20], A[20], B[20]);
  or or_30 (XOR[21], A[21], B[21]);
  or or_31 (XOR[22], A[22], B[22]);
  or or_32 (XOR[23], A[23], B[23]);
  or or_33 (OR[8], A[8], B[8]);
  or or_34 (OR[9], A[9], B[9]);
  or or_35 (OR[10], A[10], B[10]);
  or or_36 (OR[11], A[11], B[11]);
  or or_37 (OR[12], A[12], B[12]);
  or or_38 (OR[13], A[13], B[13]);
  or or_39 (OR[14], A[14], B[14]);
  or or_40 (OR[15], A[15], B[15]);
  or or_41 (XOR[24], A[24], B[24]);
  or or_42 (XOR[25], A[24], B[24]);
  or or_43 (XOR[26], A[25], B[25]);
  or or_44 (XOR[27], A[26], B[26]);
  or or_45 (XOR[28], A[27], B[28]);
  or or_46 (XOR[29], A[29], B[29]);
  or or_47 (XOR[30], A[30], B[30]);
  or or_48 (XOR[31], A[31], B[31]);
  or or_49 (OR[16], A[16], B[16]);
  or or_50 (OR[17], A[17], B[17]);
  or or_51 (OR[18], A[18], B[18]);
  or or_52 (OR[19], A[19], B[19]);
  or or_53 (OR[20], A[20], B[20]);
  or or_54 (OR[21], A[21], B[21]);
  or or_55 (OR[22], A[22], B[22]);
  or or_56 (OR[23], A[23], B[23]);
  or or_57 (OR[24], A[24], B[24]);
  or or_58 (OR[25], A[24], B[24]);
  or or_59 (OR[26], A[25], B[25]);
  or or_60 (OR[27], A[26], B[26]);
  or or_61 (OR[28], A[27], B[28]);
  or or_62 (OR[29], A[29], B[29]);
  or or_63 (OR[30], A[30], B[30]);
  or or_64 (OR[31], A[31], B[31]);

  // Other names for the same wires on the sheet: _0A = A[0]; _1A = A[1]; _2A = A[2]; _3A = A[3]; _4A = A[4];
  //   _5A = A[5]; _6A = A[6]; _7A = A[7]; _8A = A[8]; _9A = A[9]; _10A = A[10]; _11A = A[11]; _12A = A[12];
  //   _13A = A[13]; _14A = A[14]; _15A = A[15]; _16A = A[16]; _17A = A[17]; _18A = A[18]; _19A = A[19]; _20A = A[20];
  //   _21A = A[21]; _22A = A[22]; _23A = A[23]; _24A = A[24]; _25A = A[25]; _26A = A[26]; _27A = A[27]; _28A = A[28];
  //   _29A = A[29]; _30A = A[30]; _31A = A[31]; _0B = B[0]; _1B = B[1]; _2B = B[2]; _3B = B[3]; _4B = B[4];
  //   _5B = B[5]; _6B = B[6]; _7B = B[7]; _8B = B[8]; _9B = B[9]; _10B = B[10]; _11B = B[11]; _12B = B[12];
  //   _13B = B[13]; _14B = B[14]; _15B = B[15]; _16B = B[16]; _17B = B[17]; _18B = B[18]; _19B = B[19]; _20B = B[20];
  //   _21B = B[21]; _22B = B[22]; _23B = B[23]; _24B = B[24]; _25B = B[25]; _26B = B[26]; _27B = B[27]; _28B = B[28];
  //   _29B = B[29]; _30B = B[30]; _31B = B[31]

  // Notes on the sheet:
  //   ENTRADA
  //   AND
  //   HACE TODAS LAS OPERACIONES LOGICAS
  //   BIT A BIT ENTRE DOS ENTRADAS
  //   XOR
  //   OR
  //   SALIDA
endmodule

module Branch_control (
  input  CLK,
  input  RST,
  input  [31:0] Jump_size,
  input  INSTRUC,
  input  COND,
  output [31:0] Output
);

  wire and_1_out;
  wire [31:0] adder_1_out, adder_2_out, multiplexer_1_out, multiplier_1_out;

  Multiplier #(.width(32)) multiplier_1 (.a(32'h4), .b(Jump_size), .out(multiplier_1_out));  // open: cin, cout
  Adder #(.width(32)) adder_1 (.a(Output), .b(32'h4), .out(adder_1_out));  // open: cin, cout
  Multiplexer #(.width(32)) multiplexer_1 (
    .in0({32{1'b0}}), .in1(multiplier_1_out), .out(multiplexer_1_out), .sel(and_1_out));  // open: en
  and and_1 (and_1_out, INSTRUC, COND);
  Adder #(.width(32)) adder_2 (.a(adder_1_out), .b(multiplexer_1_out), .out(adder_2_out));  // open: cin, cout
  Register #(.width(32)) register_1 (.D(adder_2_out), .en(1'b1), .Q(Output), .clk(CLK), .clr(RST));

  // Notes on the sheet:
  //   MULT X4
  //   TAMAÑO
  //   DEL SALTO
  //   SUMA 4
  //   SALTO
  //   BRANCH CONTROL
  //   SALTO
  //   SUMA SALTO
  //   CONTADOR
  //   PROXIMA
  //   INSTRUCCION
endmodule

module READ_AND_WRITE (
  input  [31:0] in_1,
  input  [31:0] in_2,
  input  in_3,
  input  in_4,
  input  [31:0] in_5,
  input  [4:0] in_6,
  output [31:0] out_7,
  output [31:0] out_8,
  output [31:0] Output,
  output [31:0] out_10,
  output [31:0] out_11
);

  wire or_1_out, or_2_out, push, sw;
  wire [31:0] adder_1_out, B, multiplexer_1_out, multiplexer_2_out;

  Comparator #(.width(5)) comparator_1 (.a(5'b10111), .b(in_6), .eq(sw));  // open: gt, lt
  Comparator #(.width(5)) comparator_2 (.a(5'b11001), .b(in_6), .eq(push));  // open: gt, lt
  Adder #(.width(32)) adder_1 (.a(in_2), .b({{17{in_1[15]}}, in_1[14:0]}), .out(adder_1_out));  // open: cin, cout
  Multiplexer #(.width(32), .enable("false")) multiplexer_1 (
    .in0(adder_1_out), .in1(B), .out(multiplexer_1_out), .sel(push));
  or or_1 (or_1_out, push, sw);
  Register #(.width(32)) register_1 (.D(multiplexer_1_out), .en(or_1_out), .Q(Output), .clk(in_3), .clr(in_4));
  Multiplexer #(.width(32), .enable("false")) multiplexer_2 (.in0(in_2), .in1(B), .out(multiplexer_2_out), .sel(sw));
  Register #(.width(32)) register_2 (.D(multiplexer_2_out), .en(or_2_out), .Q(out_7), .clk(in_3), .clr(in_4));
  or or_2 (or_2_out, sw, push);

  assign out_8 = out_7;
  assign out_10 = out_7;
  assign out_11 = out_7;

  // Other names for the same wires on the sheet: A[31:0] = in_2; CLK = in_3; k[31:0] = {{17{in_1[15]}}, in_1[14:0]};
  //   op[4:0] = in_6; RST = in_4

  // Notes on the sheet:
  //   WRITER
endmodule
